// Logisim project ORDINATEUR.circ as structural Verilog: 5 circuits, main circuit main
module main (
  input  Reset
);

  wire clock_1_out, control_unit_1_ac_clr, control_unit_1_ac_ld, control_unit_1_alu_add,
       control_unit_1_alu_and, control_unit_1_alu_cma, control_unit_1_alu_reg, control_unit_1_ar_inc,
       control_unit_1_ar_ld, control_unit_1_dr_inc, control_unit_1_dr_ld, control_unit_1_e_clr,
       control_unit_1_fgi_clr, control_unit_1_fgo_clr, control_unit_1_i_clr, control_unit_1_i_set,
       control_unit_1_ir_ld, control_unit_1_m_read, control_unit_1_m_write, control_unit_1_outr_ld,
       control_unit_1_pc_inc, control_unit_1_pc_ld, control_unit_1_s0, control_unit_1_s1, control_unit_1_s2,
       control_unit_1_s_clr, control_unit_1_x, d_ff_1_q, data_unit_1_fgi, data_unit_1_fgo, data_unit_1_s,
       data_unit_1_z, i_o_interface_module_1_fgi_set, i_o_interface_module_1_fgo_set,
       i_o_interface_module_1_input_ready, i_o_interface_module_1_output_ready, INPUT_BOUTON_out,
       ON_BUTTON_out, or_1_out, or_2_out, or_3_out, OUTPUT_BOUTON_out;
  wire [3:0] control_unit_1_opcode;
  wire [7:0] data_unit_1_output_reg, dipswitch_1_sw8, i_o_interface_module_1_cu_input,
       i_o_interface_module_1_output_out;
  wire [15:0] data_unit_1_ir_out;

  Button ON_BUTTON (.out(ON_BUTTON_out));
  Button INPUT_BOUTON (.out(INPUT_BOUTON_out));
  Button OUTPUT_BOUTON (.out(OUTPUT_BOUTON_out));
  D_Flip_Flop d_ff_1 (.D(ON_BUTTON_out), .clk(ON_BUTTON_out), .Q(d_ff_1_q), .reset(data_unit_1_s));  // open: Qn, preset
  DipSwitch dipswitch_1 (
    .sw1(dipswitch_1_sw8[7]), .sw2(dipswitch_1_sw8[6]), .sw3(dipswitch_1_sw8[5]), .sw4(dipswitch_1_sw8[4]),
    .sw5(dipswitch_1_sw8[3]), .sw6(dipswitch_1_sw8[2]), .sw7(dipswitch_1_sw8[1]), .sw8(dipswitch_1_sw8[0]));
  Clock clock_1 (.out(clock_1_out));
  LED INPUT_READY (.in(i_o_interface_module_1_input_ready));
  LED OUTPUT_READY (.in(i_o_interface_module_1_output_ready));
  Control_Unit control_unit_1 (
    .Instruction_Register(data_unit_1_ir_out), .CLK(clock_1_out), .S(data_unit_1_s), .Z(data_unit_1_z),
    .FGI(data_unit_1_fgi), .FGO(data_unit_1_fgo), .RESET(Reset), .S2(control_unit_1_s2),
    .S1(control_unit_1_s1), .S0(control_unit_1_s0), .AR_LD(control_unit_1_ar_ld),
    .AR_INC(control_unit_1_ar_inc), .PC_LD(control_unit_1_pc_ld), .PC_INC(control_unit_1_pc_inc),
    .IR_LD(control_unit_1_ir_ld), .AC_LD(control_unit_1_ac_ld), .AC_CLR(control_unit_1_ac_clr),
    .DR_LD(control_unit_1_dr_ld), .DR_INC(control_unit_1_dr_inc), .X(control_unit_1_x),
    .ALU_AND(control_unit_1_alu_and), .ALU_ADD(control_unit_1_alu_add), .ALU_CMA(control_unit_1_alu_cma),
    .ALU_REG(control_unit_1_alu_reg), .M_Read(control_unit_1_m_read), .M_Write(control_unit_1_m_write),
    .S_CLR(control_unit_1_s_clr), .E_CLR(control_unit_1_e_clr), .I_SET(control_unit_1_i_set),
    .I_CLR(control_unit_1_i_clr), .FGI_CLR(control_unit_1_fgi_clr), .FGO_CLR(control_unit_1_fgo_clr),
    .OUTR_LD(control_unit_1_outr_ld), .opcode(control_unit_1_opcode));  // open: INPR_LD
  I_O_Interface_Module i_o_interface_module_1 (
    .button_input(INPUT_BOUTON_out), .button_output(OUTPUT_BOUTON_out), .RES_SIG(or_3_out),
    .opcode(control_unit_1_opcode), .INPUT_IN(dipswitch_1_sw8), .CU_OUTPUT(data_unit_1_output_reg),
    .FGI_SET(i_o_interface_module_1_fgi_set), .FGO_SET(i_o_interface_module_1_fgo_set),
    .INPUT_READY(i_o_interface_module_1_input_ready), .OUTPUT_READY(i_o_interface_module_1_output_ready),
    .CU_INPUT(i_o_interface_module_1_cu_input), .OUTPUT_OUT(i_o_interface_module_1_output_out));
  LED led_1 (.in(i_o_interface_module_1_output_out[7]));
  or or_1 (or_1_out, control_unit_1_ac_clr, Reset);
  or or_2 (or_2_out, control_unit_1_s_clr, Reset);
  LED led_2 (.in(i_o_interface_module_1_output_out[6]));
  LED led_3 (.in(i_o_interface_module_1_output_out[5]));
  LED led_4 (.in(i_o_interface_module_1_output_out[4]));
  LED led_5 (.in(i_o_interface_module_1_output_out[3]));
  LED led_6 (.in(i_o_interface_module_1_output_out[2]));
  LED led_7 (.in(i_o_interface_module_1_output_out[1]));
  LED led_8 (.in(i_o_interface_module_1_output_out[0]));
  Data_Unit data_unit_1 (
    .CLK(clock_1_out), .S2(control_unit_1_s2), .ALU_REG(control_unit_1_alu_reg),
    .AR_LD(control_unit_1_ar_ld), .PC_LD(control_unit_1_pc_ld), .DR_INC(control_unit_1_dr_inc),
    .AC_CLR(or_1_out), .FGI_SET(i_o_interface_module_1_fgi_set), .I_SET(control_unit_1_i_set),
    .PC_INC(control_unit_1_pc_inc), .ON_BUTTON(d_ff_1_q), .S_CLR(or_2_out), .ALU_CMP(control_unit_1_alu_cma),
    .DR_CLR(Reset), .FGI_CLR(control_unit_1_fgi_clr), .S0(control_unit_1_s0), .PC_CLR(Reset), .AR_CLR(Reset),
    .ALU_AND(control_unit_1_alu_and), .IR_LD(control_unit_1_ir_ld), .I_CLR(control_unit_1_i_clr),
    .AC_LD(control_unit_1_ac_ld), .M_READ(control_unit_1_m_read), .S1(control_unit_1_s1),
    .X(control_unit_1_x), .ALU_ADD(control_unit_1_alu_add), .AR_INC(control_unit_1_ar_inc),
    .DR_LD(control_unit_1_dr_ld), .M_WRITE(control_unit_1_m_write), .FGO_SET(i_o_interface_module_1_fgo_set),
    .FGO_CLR(control_unit_1_fgo_clr), .INPUT_REG(i_o_interface_module_1_cu_input), .INPR_LD(or_3_out),
    .OUTR_LD(control_unit_1_outr_ld), .S(data_unit_1_s), .IR_OUT(data_unit_1_ir_out), .Z(data_unit_1_z),
    .FGI(data_unit_1_fgi), .FGO(data_unit_1_fgo), .OUTPUT_REG(data_unit_1_output_reg),
    .E_CLR(control_unit_1_e_clr));  // open: S_CMP, Z_CMP, I_CMP, E_CMP, FGI_CMP, FGO_CMP, E, I
  or or_3 (or_3_out, data_unit_1_fgo, data_unit_1_fgi);
endmodule

module Control_Unit (
  input  [15:0] Instruction_Register,
  input  CLK,
  input  S,
  input  Z,
  input  FGI,
  input  FGO,
  input  RESET,
  output S2,
  output S1,
  output S0,
  output AR_LD,
  output AR_INC,
  output PC_LD,
  output PC_INC,
  output IR_LD,
  output AC_LD,
  output AC_CLR,
  output DR_LD,
  output DR_INC,
  output X,
  output ALU_AND,
  output ALU_ADD,
  output ALU_CMA,
  output ALU_REG,
  output M_Read,
  output M_Write,
  output S_CLR,
  output E_CLR,
  output I_SET,
  output I_CLR,
  output FGI_CLR,
  output FGO_CLR,
  output INPR_LD,
  output OUTR_LD,
  output [3:0] opcode
);

  wire and_1_out, and_2_out, and_5_out, and_6_out, D0T4_out, D0T5_out, D1T4_out, D3T4_out, D4T4_out,
       D7T4_out, D7T6_out, D7T7_out, D8T4_out, D9T5_out, D13T4_out, D14T4_out, d_ff_1_q, decoder_1_out0,
       decoder_1_out1, decoder_1_out3, decoder_1_out4, decoder_1_out5, decoder_1_out6, decoder_1_out7,
       decoder_1_out8, decoder_1_out9, decoder_1_out10, decoder_1_out11, decoder_1_out12, decoder_1_out13,
       decoder_1_out14, decoder_1_out15, decoder_2_out0, decoder_2_out2, decoder_2_out3, decoder_2_out4,
       decoder_2_out5, decoder_2_out6, decoder_2_out7, IT3_out, not_1_out, not_2_out, or_1_out, or_13_out;
  wire [2:0] Sequence_Counter_q;

  D_Flip_Flop d_ff_1 (.D(or_13_out), .clk(and_1_out), .Q(d_ff_1_q), .reset(not_1_out));  // open: Qn, preset
  not not_1 (not_1_out, or_13_out);
  and and_1 (and_1_out, CLK, S);
  or or_1 (or_1_out, d_ff_1_q, RESET);
  Counter #(.width(3), .max('h7)) Sequence_Counter (
    .clr(or_1_out), .load(1'b0), .up(1'b1), .count(1'b1), .clk(and_1_out), .Q(Sequence_Counter_q));  // open: D, carry
  Decoder #(.select(4), .enable("false")) decoder_1 (
    .out0(decoder_1_out0), .out1(decoder_1_out1), .out3(decoder_1_out3), .out4(decoder_1_out4),
    .out5(decoder_1_out5), .out6(decoder_1_out6), .out7(decoder_1_out7), .out8(decoder_1_out8),
    .out9(decoder_1_out9), .out10(decoder_1_out10), .out11(decoder_1_out11), .out12(decoder_1_out12),
    .out13(decoder_1_out13), .out14(decoder_1_out14), .out15(decoder_1_out15),
    .sel(Instruction_Register[15:12]));  // open: out2
  Decoder #(.select(3), .enable("false")) decoder_2 (
    .out0(decoder_2_out0), .out1(IR_LD), .out2(decoder_2_out2), .out3(decoder_2_out3), .out4(decoder_2_out4),
    .out5(decoder_2_out5), .out6(decoder_2_out6), .out7(decoder_2_out7), .sel(Sequence_Counter_q));
  and IT3 (IT3_out, Instruction_Register[11], decoder_2_out3);
  and D0T4 (D0T4_out, decoder_1_out0, decoder_2_out4);
  and D0T5 (D0T5_out, decoder_1_out0, decoder_2_out5);
  and D1T4 (D1T4_out, decoder_1_out1, decoder_2_out4);
  and D3T4 (D3T4_out, decoder_1_out3, decoder_2_out4);
  and D3T5 (ALU_ADD, decoder_1_out3, decoder_2_out5);
  and D4T4 (D4T4_out, decoder_1_out4, decoder_2_out4);
  and D4T5 (ALU_AND, decoder_1_out4, decoder_2_out5);
  and D5T4 (ALU_CMA, decoder_1_out5, decoder_2_out4);
  and D6T4 (AC_CLR, decoder_1_out6, decoder_2_out4);
  and D7T4 (D7T4_out, decoder_1_out7, decoder_2_out4);
  and D7T5 (DR_INC, decoder_1_out7, decoder_2_out5);
  and D7T6 (D7T6_out, decoder_1_out7, decoder_2_out6);
  and D7T7 (D7T7_out, decoder_1_out7, decoder_2_out7);
  and D8T4 (D8T4_out, decoder_1_out8, decoder_2_out4);
  and D9T4 (AR_INC, decoder_1_out9, decoder_2_out4);
  and D9T5 (D9T5_out, decoder_1_out9, decoder_2_out5);
  and D10T4 (E_CLR, decoder_1_out10, decoder_2_out4);
  and D11T4 (FGI_CLR, decoder_1_out11, decoder_2_out4);
  and D12T4 (FGO_CLR, decoder_1_out12, decoder_2_out4);
  and D13T4 (D13T4_out, decoder_1_out13, decoder_2_out4);
  and D14T4 (D14T4_out, decoder_1_out14, decoder_2_out4);
  and D15T4 (S_CLR, decoder_1_out15, decoder_2_out4);
  not not_2 (not_2_out, Instruction_Register[11]);
  and and_2 (and_2_out, D7T7_out, Z);
  and and_3 (I_SET, Instruction_Register[11], decoder_2_out2);
  and and_4 (I_CLR, not_2_out, decoder_2_out2);
  and and_5 (and_5_out, D13T4_out, FGI);
  and and_6 (and_6_out, D14T4_out, FGO);
  or or_2 (S2, decoder_2_out0, IR_LD, IT3_out, D0T4_out, D3T4_out, D4T4_out, D7T4_out, D8T4_out, AR_INC, D9T5_out);
  or or_3 (S1, IR_LD, decoder_2_out2, IT3_out, D0T4_out, D1T4_out, D3T4_out, D4T4_out, D7T4_out, FGO_CLR);
  or or_4 (S0, decoder_2_out2, D7T6_out, D8T4_out, D9T5_out);
  or or_5 (AR_LD, decoder_2_out0, decoder_2_out2, IT3_out);
  or or_6 (PC_LD, D8T4_out, D9T5_out);
  or or_7 (PC_INC, IR_LD, and_2_out, and_5_out, and_6_out);
  or or_8 (AC_LD, ALU_AND, D0T5_out, ALU_ADD, ALU_CMA, D7T6_out, FGI_CLR);
  or or_9 (DR_LD, D0T4_out, D3T4_out, D4T4_out, D7T4_out);
  or or_10 (ALU_REG, D0T5_out, D7T6_out, FGI_CLR);
  or or_11 (M_Read, IR_LD, IT3_out, D0T4_out, D7T4_out, D3T4_out, D4T4_out);
  or or_12 (M_Write, D7T6_out, D1T4_out, AR_INC);
  or or_13 (or_13_out, D0T5_out, D1T4_out, ALU_ADD, S_CLR, ALU_AND, ALU_CMA, AC_CLR, D14T4_out, D7T7_out, D8T4_out, D9T5_out, FGO_CLR, E_CLR, FGI_CLR, D13T4_out);

  assign INPR_LD = FGI_CLR;
  assign opcode = Instruction_Register[15:12];
  assign OUTR_LD = FGO_CLR;
  assign X = FGI_CLR;
endmodule

module Data_Unit (
  input  AR_LD,
  input  AR_CLR,
  input  ON_BUTTON,
  input  AR_INC,
  input  ALU_ADD,
  input  S_CLR,
  input  ALU_AND,
  input  S_CMP,
  input  PC_LD,
  input  PC_CLR,
  input  E_CLR,
  input  PC_INC,
  input  E_CMP,
  input  X,
  input  ALU_CMP,
  input  IR_LD,
  input  ALU_REG,
  input  Z_CMP,
  input  S0,
  input  I_SET,
  input  DR_LD,
  input  S1,
  input  DR_CLR,
  input  I_CLR,
  input  S2,
  input  DR_INC,
  input  I_CMP,
  input  FGI_SET,
  input  M_WRITE,
  input  M_READ,
  input  FGI_CLR,
  input  AC_LD,
  input  CLK,
  input  AC_CLR,
  input  FGI_CMP,
  input  FGO_SET,
  input  FGO_CLR,
  input  [7:0] INPUT_REG,
  input  FGO_CMP,
  input  INPR_LD,
  input  OUTR_LD,
  output S,
  output E,
  output [15:0] IR_OUT,
  output Z,
  output I,
  output FGI,
  output FGO,
  output [7:0] OUTPUT_REG
);

  wire alu_1_e_clr, alu_1_e_set, decoder_1_out1, decoder_1_out2, decoder_1_out3, decoder_1_out4,
       decoder_1_out5, decoder_1_out6, not_1_out, or_1_out, or_2_out, or_3_out, or_4_out, or_5_out, or_6_out,
       or_7_out, or_8_out, or_9_out, or_10_out, or_11_out, or_12_out, or_13_out, or_14_out, or_15_out,
       or_16_out, or_17_out, or_18_out;
  wire [7:0] controlled_buffer_7_out, controlled_buffer_8_out, INPR_q, undriven;
  wire [10:0] adder_1_out, adder_2_out, AR_q, controlled_buffer_2_out, controlled_buffer_3_out, PC_q;
  wire [15:0] AC_q, adder_3_out, alu_1_ac_out, controlled_buffer_1_out, controlled_buffer_4_out,
       controlled_buffer_5_out, controlled_buffer_6_out, DR_q, multiplexer_1_out, RAM_MEMORY_dout;

  RAM #(.addrWidth(11), .dataWidth(16), .trigger("falling"), .databus("bibus")) RAM_MEMORY (
    .addr(AR_q), .we(M_WRITE), .oe(M_READ), .clk(CLK), .din(controlled_buffer_1_out), .dout(RAM_MEMORY_dout));
  Multiplexer #(.width(16), .enable("false")) multiplexer_1 (
    .in0(DR_q), .in1({undriven, INPR_q}), .out(multiplexer_1_out), .sel(X));
  ALU alu_1 (
    .REG_IN(multiplexer_1_out), .AC(AC_q), .ALU_ADD(ALU_ADD), .ALU_AND(ALU_AND), .ALU_CMP(ALU_CMP),
    .ALU_REG(ALU_REG), .AC_OUT(alu_1_ac_out), .E_SET(alu_1_e_set), .E_CLR(alu_1_e_clr));
  Decoder #(.select(3), .enable("false")) decoder_1 (
    .out1(decoder_1_out1), .out2(decoder_1_out2), .out3(decoder_1_out3), .out4(decoder_1_out4),
    .out5(decoder_1_out5), .out6(decoder_1_out6), .sel({S2, S1, S0}));  // open: out0, out7
  assign controlled_buffer_1_out = decoder_1_out6 ? RAM_MEMORY_dout : 16'bz;  // Controlled_Buffer controlled_buffer_1
  assign controlled_buffer_2_out = AR_LD ? controlled_buffer_1_out[10:0] : 11'bz;  // Controlled_Buffer controlled_buffer_2
  assign controlled_buffer_3_out = PC_LD ? controlled_buffer_1_out[10:0] : 11'bz;  // Controlled_Buffer controlled_buffer_3
  assign controlled_buffer_4_out = IR_LD ? controlled_buffer_1_out : 16'bz;  // Controlled_Buffer controlled_buffer_4
  assign controlled_buffer_5_out = DR_LD ? controlled_buffer_1_out : 16'bz;  // Controlled_Buffer controlled_buffer_5
  assign controlled_buffer_6_out = AC_LD ? alu_1_ac_out : 16'bz;  // Controlled_Buffer controlled_buffer_6
  assign controlled_buffer_7_out = INPR_LD ? INPUT_REG : 8'bz;  // Controlled_Buffer controlled_buffer_7
  assign controlled_buffer_8_out = OUTR_LD ? controlled_buffer_1_out[7:0] : 8'bz;  // Controlled_Buffer controlled_buffer_8
  Register #(.width(11)) AR (.D(controlled_buffer_2_out), .en(or_1_out), .clk(CLK), .Q(AR_q), .clr(AR_CLR));
  or or_1 (or_1_out, AR_LD, AR_CLR, AR_INC);
  assign controlled_buffer_2_out = AR_INC ? adder_1_out : 11'bz;  // Controlled_Buffer controlled_buffer_9
  Adder #(.width(11)) adder_1 (.a(AR_q), .b(11'h1), .out(adder_1_out));  // open: cin, cout
  Register #(.width(11)) PC (.D(controlled_buffer_3_out), .en(or_2_out), .clk(CLK), .Q(PC_q), .clr(PC_CLR));
  or or_2 (or_2_out, PC_LD, PC_CLR, PC_INC);
  assign controlled_buffer_3_out = PC_INC ? adder_2_out : 11'bz;  // Controlled_Buffer controlled_buffer_10
  Adder #(.width(11)) adder_2 (.a(PC_q), .b(11'h1), .out(adder_2_out));  // open: cin, cout
  Register #(.width(16)) IR (.D(controlled_buffer_4_out), .en(IR_LD), .clk(CLK), .Q(IR_OUT));  // open: clr
  Register #(.width(16)) DR (.D(controlled_buffer_5_out), .en(or_3_out), .clk(CLK), .Q(DR_q), .clr(DR_CLR));
  or or_3 (or_3_out, DR_LD, DR_CLR, DR_INC);
  assign controlled_buffer_5_out = DR_INC ? adder_3_out : 16'bz;  // Controlled_Buffer controlled_buffer_11
  Adder #(.width(16)) adder_3 (.a(DR_q), .b(16'h1), .out(adder_3_out));  // open: cin, cout
  Register #(.width(16)) AC (.D(controlled_buffer_6_out), .en(or_4_out), .clk(CLK), .Q(AC_q), .clr(AC_CLR));
  or or_4 (or_4_out, AC_LD, AC_CLR);
  Register #(.trigger("falling")) INPR (.D(controlled_buffer_7_out), .en(INPR_LD), .clk(CLK), .Q(INPR_q));  // open: clr
  Register #(.trigger("falling")) OUTR (
    .D(controlled_buffer_8_out), .en(OUTR_LD), .clk(CLK), .Q(OUTPUT_REG));  // open: clr
  assign controlled_buffer_1_out = decoder_1_out3 ? IR_OUT : 16'bz;  // Controlled_Buffer controlled_buffer_12
  assign controlled_buffer_1_out = decoder_1_out1 ? DR_q : 16'bz;  // Controlled_Buffer controlled_buffer_13
  assign controlled_buffer_1_out = decoder_1_out2 ? AC_q : 16'bz;  // Controlled_Buffer controlled_buffer_14
  assign controlled_buffer_1_out = decoder_1_out5 ? {{5{1'b0}}, AR_q} : 16'bz;  // Controlled_Buffer controlled_buffer_15
  assign controlled_buffer_1_out = decoder_1_out4 ? {{5{1'b0}}, PC_q} : 16'bz;  // Controlled_Buffer controlled_buffer_16
  or or_5 (or_5_out, AC_q[0], AC_q[1], AC_q[2], AC_q[3], AC_q[4], AC_q[5], AC_q[6], AC_q[7], AC_q[9], AC_q[10], AC_q[11], AC_q[12], AC_q[13], AC_q[14], AC_q[15], AC_q[8]);
  or or_6 (or_6_out, E_CLR, alu_1_e_clr);
  not not_1 (not_1_out, or_5_out);
  J_K_Flip_Flop S_REG (.J(or_7_out), .K(or_8_out), .clk(CLK), .Q(S));  // open: Qn, preset, reset
  or or_7 (or_7_out, ON_BUTTON, S_CMP);
  or or_8 (or_8_out, S_CLR, S_CMP);
  J_K_Flip_Flop E_REG (.J(or_9_out), .K(or_10_out), .clk(CLK), .Q(E));  // open: Qn, preset, reset
  or or_9 (or_9_out, alu_1_e_set, E_CMP);
  or or_10 (or_10_out, or_6_out, E_CMP);
  J_K_Flip_Flop #(.trigger("falling")) Z_REG (
    .J(or_11_out), .K(or_12_out), .clk(CLK), .Q(Z));  // open: Qn, preset, reset
  or or_11 (or_11_out, not_1_out, Z_CMP);
  or or_12 (or_12_out, or_5_out, Z_CMP);
  J_K_Flip_Flop I_REG (.J(or_13_out), .K(or_14_out), .clk(CLK), .Q(I));  // open: Qn, preset, reset
  or or_13 (or_13_out, I_SET, I_CMP);
  or or_14 (or_14_out, I_CLR, I_CMP);
  J_K_Flip_Flop #(.trigger("falling")) FGI_REG (
    .J(or_15_out), .K(or_16_out), .clk(CLK), .Q(FGI));  // open: Qn, preset, reset
  or or_15 (or_15_out, FGI_SET, FGI_CMP);
  or or_16 (or_16_out, FGI_CLR, FGI_CMP);
  J_K_Flip_Flop #(.trigger("falling")) FGO_REG (
    .J(or_17_out), .K(or_18_out), .clk(CLK), .Q(FGO));  // open: Qn, preset, reset
  or or_17 (or_17_out, FGO_SET, FGO_CMP);
  or or_18 (or_18_out, FGO_CLR, FGO_CMP);
endmodule

module ALU (
  input  [15:0] REG_IN,
  input  [15:0] AC,
  input  ALU_ADD,
  input  ALU_AND,
  input  ALU_CMP,
  input  ALU_REG,
  output [15:0] AC_OUT,
  output E_SET,
  output E_CLR
);

  wire adder_1_cout, not_2_out;
  wire [15:0] adder_1_out, and_1_out, not_1_out;

  assign not_1_out = ~AC;  // NOT_Gate not_1, 16 bits wide
  assign and_1_out = REG_IN & AC;  // AND_Gate and_1, 16 bits wide
  assign AC_OUT = ALU_AND ? and_1_out : 16'bz;  // Controlled_Buffer controlled_buffer_1
  Adder #(.width(16)) adder_1 (.a(REG_IN), .b(AC), .out(adder_1_out), .cout(adder_1_cout));  // open: cin
  assign AC_OUT = ALU_ADD ? adder_1_out : 16'bz;  // Controlled_Buffer controlled_buffer_2
  assign AC_OUT = ALU_CMP ? not_1_out : 16'bz;  // Controlled_Buffer controlled_buffer_3
  assign AC_OUT = ALU_REG ? REG_IN : 16'bz;  // Controlled_Buffer controlled_buffer_4
  and and_2 (E_SET, adder_1_cout, ALU_ADD);
  not not_2 (not_2_out, adder_1_cout);
  and and_3 (E_CLR, not_2_out, ALU_ADD);
endmodule

module I_O_Interface_Module (
  input  button_input,
  input  button_output,
  input  RES_SIG,
  input  [3:0] opcode,
  input  [7:0] INPUT_IN,
  input  [7:0] CU_OUTPUT,
  output FGI_SET,
  output FGO_SET,
  output INPUT_READY,
  output OUTPUT_READY,
  output [7:0] CU_INPUT,
  output [7:0] OUTPUT_OUT
);

  D_Flip_Flop input_setter (.D(button_input), .clk(button_input), .Q(FGI_SET), .reset(RES_SIG));  // open: Qn, preset
  D_Flip_Flop output_setter (.D(button_output), .clk(button_output), .Q(FGO_SET), .reset(RES_SIG));  // open: Qn, preset
  and and_1 (INPUT_READY, opcode[0], ~opcode[1], opcode[2], opcode[3]);  // AND_Gate
  and and_2 (OUTPUT_READY, ~opcode[0], opcode[1], opcode[2], opcode[3]);  // AND_Gate

  assign CU_INPUT = INPUT_IN;
  assign OUTPUT_OUT = CU_OUTPUT;
endmodule
